# Fritzing sketch imperial (saved by Fritzing 0.9.2b)
circuit board: 8.46667cm x 5.64444cm
breadboards: 1

parts:
  U1 = attiny85 [package=dip]
  SW = Momentary Switch [package=ksa_sealed_tac_switch]
  B = Piezo Speaker
  BAT = Battery Holders [package=battcom_20mm_pth]
  R = Resistor [tolerance=±5% resistance=100 package=THT]

nets:
  N1: U1.Pin_4, B.pin1, BAT.-
  N2: U1.Pin_6, R.Pin_1
  N3: U1.Pin_8, SW.3
  N4: SW.1, BAT.+
  N5: B.pin2, R.Pin_0
